# Fritzing sketch Little Kitchen (saved by Fritzing 0.9.3b)
breadboards: 1

parts:
  Onderdeel1 = Arduino Mega 2560 (Rev3)
  LedOn = LED - 5mm [color="Red (633nm)" package="5 mm [THT]"]
  BtnOn = Pushbutton [package=THT]
  R1 = Resistor [tolerance=±5% resistance=220 package=THT]
  R2 = Resistor [tolerance=±5% resistance=10k package=THT]
  MCP1 = MCP23016 [package="DIP (Dual Inline) [THT]"]  # not connected
  IC1 = FRM010 [package=THT]

nets:
  N1: Onderdeel1.5V, BtnOn.leg1
  N2: Onderdeel1.GND, BtnOn.leg0, R1.Pin_1, R2.Pin_0
  N3: Onderdeel1.D22, LedOn.anode
  N4: Onderdeel1.D24, R2.Pin_1
  N5: LedOn.cathode, R1.Pin_0
  N6: IC1.LCD_RS, IC1.LCD_PWR
  N7: IC1.LCD_E, IC1.LED
  N8: IC1.Serial_In, IC1.XTAL#15
  N9: IC1.Reset, IC1.XTAL#14
  N10: IC1.0V, IC1.+V
  N11: IC1.LCD_D4, IC1.JP4_-_Number_of_Lines_selection
  N12: IC1.LCD_D5, IC1.JP3_-_Polarity_selection
  N13: IC1.LCD_D6, IC1.JP2_-_Baud_Rate_selection
  N14: IC1.LCD_D7, IC1.JP1_-_Welcome_Message_selection

custom parts:
  MCP23016: An I2C BUS 16 bit I/O expander.
